# Fritzing sketch RelayBoard (saved by Fritzing 0.8.5b)
circuit board: 5.52611cm x 5.19726cm
breadboards: 1

parts:
  J1 = female pin header, 3 pins [form="♀ (female)"]
  K1 = Relay [part_number=FRS1B-S package=THT]
  LED1 = LED - 5mm [color="Red (633nm)" package="5 mm [THT]"]
  RL = Resistor [tolerance=±5% resistance=220 package=THT]
  Q1 = NPN-Transistor [package="TO92 [THT]"]
  RT = Resistor [tolerance=±5% resistance=1k package=THT]
  RR = Resistor [tolerance=±5% resistance=220 package=THT]
  D1 = Rectifier Diode [part_number=1N4001 package="300 mil [THT]"]

nets:
  N1: J1.pin1, RL.Pin_1, RR.Pin_1
  N2: J1.pin2, LED1.anode, Q1.B, RT.Pin_0, RT.Pin_1
  N3: J1.pin3, Q1.C
  N4: K1.COIL1, RR.Pin_0, D1.anode
  N5: K1.C1, K1.C2
  N6: K1.COIL2, Q1.E, D1.cathode
  N7: LED1.cathode, RL.Pin_0

notes:
  1. GND
  2. IN: changes relay state
  3. VCC, 5V
